# Fritzing sketch AzteXMotors (saved by Fritzing 0.9.1b)

parts:
  M4 = Stepper Motor - Bipolar
  MDE = Stepper Motor Header [form="♀ (female)" package=screwterminal-3.5mm-4_lock]

nets:
  N1: M4.A, MDE.1A
  N2: M4.C, MDE.1B
  N3: M4.B, MDE.2A
  N4: M4.D, MDE.2B

custom parts:
  Stepper Motor Header: 4-pin screw terminal for a stepper motor driver. Source: Header 4 Standard 4-pin 0.1 header. Use with straight break away headers (SKU : PRT-00116), right angle break away headers (PRT-00553), swiss pins (PRT-00743), machine pins (PRT-00117), and female headers (PRT-00115). Molex polarized connector foot print use with SKU : PRT-08231 with associated crimp pins and housings. 1MM SMD Version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
